// Logisim project MyCPU.circ as structural Verilog: 4 circuits, main circuit CPU
module CPU (
);

  wire clock_1_out, controll_unit_1_eac, controll_unit_1_ear, controll_unit_1_edr, controll_unit_1_ein,
       controll_unit_1_eir, controll_unit_1_eout, controll_unit_1_incpc, controll_unit_1_loadm,
       controll_unit_1_loadpc, controll_unit_1_sac, controll_unit_1_sar, controll_unit_1_sdr,
       controll_unit_1_sinr, controll_unit_1_sir, controll_unit_1_sm, controll_unit_1_spc,
       controll_unit_1_stmp, controll_unit_1_storem;
  wire [2:0] controll_unit_1_alu_control, priority_encoder_1_out;
  wire [3:0] IR_q;
  wire [11:0] AR_q, IR_q_2, PC_q;
  wire [15:0] AC_q, alu_1_out, bit_extender_1_out, bit_extender_2_out, DR_q, INP_q, multiplexer_1_out,
       ram_1_data, TMP_q;

  Controll_Unit controll_unit_1 (
    .IR_12_15(IR_q), .Clock(clock_1_out), .AC_Input(AC_q), .ALU_Control(controll_unit_1_alu_control),
    .StoreM(controll_unit_1_storem), .LoadM(controll_unit_1_loadm), .EAR(controll_unit_1_ear),
    .LoadPC(controll_unit_1_loadpc), .IncPC(controll_unit_1_incpc), .EIR(controll_unit_1_eir),
    .EDR(controll_unit_1_edr), .EAC(controll_unit_1_eac), .EIN(controll_unit_1_ein),
    .EOUT(controll_unit_1_eout), .SM(controll_unit_1_sm), .SAR(controll_unit_1_sar),
    .SPC(controll_unit_1_spc), .SIR(controll_unit_1_sir), .SDR(controll_unit_1_sdr),
    .SAC(controll_unit_1_sac), .SINR(controll_unit_1_sinr), .STMP(controll_unit_1_stmp));
  // Probe on {IR_q, IR_q_2}
  ALU alu_1 (.A(DR_q), .B(AC_q), .Operation(controll_unit_1_alu_control), .Out(alu_1_out));
  // Probe on IR_q
  Register #(.width(12)) AR (
    .D(multiplexer_1_out[11:0]), .en(controll_unit_1_ear), .Q(AR_q), .clk(clock_1_out));  // open: clr
  Counter #(.width(12), .max('hfff)) PC (
    .load(controll_unit_1_loadpc), .D(multiplexer_1_out[11:0]), .count(controll_unit_1_incpc), .Q(PC_q),
    .clk(clock_1_out));  // open: carry, clr
  Register #(.width(16)) IR (
    .D(multiplexer_1_out), .en(controll_unit_1_eir), .Q({IR_q, IR_q_2}), .clk(clock_1_out));  // open: clr
  Register #(.width(16)) DR (
    .D(multiplexer_1_out), .en(controll_unit_1_edr), .Q(DR_q), .clk(clock_1_out));  // open: clr
  Register #(.width(16)) AC (.D(alu_1_out), .en(controll_unit_1_eac), .Q(AC_q), .clk(clock_1_out));  // open: clr
  Register #(.width(16)) INP (.en(controll_unit_1_ein), .Q(INP_q), .clk(clock_1_out));  // open: D, clr
  Register #(.width(16)) OUT (.D(multiplexer_1_out), .en(controll_unit_1_eout), .clk(clock_1_out));  // open: Q, clr
  Register #(.width(16)) TMP (.D(multiplexer_1_out), .Q(TMP_q), .clk(clock_1_out));  // open: en, clr
  RAM #(.addrWidth(12), .dataWidth(16), .bus("separate")) ram_1 (
    .addr(AR_q), .din(multiplexer_1_out), .data(ram_1_data), .str(controll_unit_1_storem), .sel(1'b1),
    .clk(clock_1_out), .ld(controll_unit_1_loadm));  // open: clr
  Priority_Encoder priority_encoder_1 (
    .in0(controll_unit_1_sm), .in1(controll_unit_1_sar), .in2(controll_unit_1_spc),
    .in3(controll_unit_1_sir), .in4(controll_unit_1_sdr), .in5(controll_unit_1_sac),
    .in6(controll_unit_1_sinr), .in7(controll_unit_1_stmp), .out(priority_encoder_1_out), .en_in(1'b1));  // open: gs, en_out
  assign bit_extender_1_out = {{4{1'b0}}, AR_q};  // Bit_Extender bit_extender_1
  assign bit_extender_2_out = {{4{1'b0}}, PC_q};  // Bit_Extender bit_extender_2
  // Probe on priority_encoder_1_out
  Clock clock_1 (.out(clock_1_out));
  Multiplexer #(.select(3), .width(16), .disabled(0), .enable("false")) multiplexer_1 (
    .in0(ram_1_data), .in1(bit_extender_1_out), .in2(bit_extender_2_out), .in3({IR_q, IR_q_2}), .in4(DR_q),
    .in5(AC_q), .in6(INP_q), .in7(TMP_q), .out(multiplexer_1_out), .sel(priority_encoder_1_out));
endmodule

module ALU (
  input  [15:0] A,
  input  [15:0] B,
  input  [2:0] Operation,
  output [15:0] Out
);

  wire [15:0] adder_1_out, and_1_out, not_1_out, shifter_1_out;

  Adder #(.width(16)) adder_1 (.a(A), .b(B), .out(adder_1_out));  // open: cin, cout
  assign and_1_out = A & B;  // AND_Gate and_1, 16 bits wide
  assign not_1_out = ~B;  // NOT_Gate not_1, 16 bits wide
  Shifter #(.width(16)) shifter_1 (.in(B), .\dist (4'b0001), .out(shifter_1_out));
  Multiplexer #(.select(3), .width(16)) multiplexer_1 (
    .in0(adder_1_out), .in1(and_1_out), .in2(not_1_out), .in3(shifter_1_out), .in4(A), .out(Out),
    .sel(Operation), .en(1'b1));  // open: in5, in6, in7
endmodule

// Control Unit
module Controll_Unit (
  input  [3:0] IR_12_15,
  input  Clock,
  input  [15:0] AC_Input,
  output StoreM,
  output LoadM,
  output EAR,
  output LoadPC,
  output IncPC,
  output EIR,
  output EDR,
  output EAC,
  output EIN,
  output EOUT,
  output SM,
  output SAR,
  output SPC,
  output SIR,
  output SDR,
  output SAC,
  output SINR,
  output STMP,
  output [2:0] ALU_Control
);

  wire and_2_out, and_3_out, and_4_out, and_5_out, and_6_out, and_7_out, and_8_out, and_9_out, and_10_out,
       and_11_out, and_12_out, and_13_out, and_14_out, and_15_out, and_16_out, and_17_out, and_18_out,
       and_19_out, and_20_out, and_21_out, and_22_out, and_23_out, and_24_out, and_25_out, and_26_out,
       and_27_out, and_28_out, and_29_out, and_30_out, and_31_out, and_32_out, and_33_out, and_34_out,
       and_35_out, and_36_out, and_37_out, and_38_out, and_39_out, and_40_out, and_41_out, and_42_out,
       and_43_out, and_44_out, and_45_out, and_46_out, and_47_out, and_48_out, and_49_out, and_52_out,
       and_53_out, and_54_out, and_55_out, and_56_out, and_57_out, and_58_out, and_59_out, and_60_out,
       and_61_out, and_62_out, and_63_out, and_64_out, decoder_1_out0, decoder_1_out1, decoder_1_out2,
       decoder_1_out3, decoder_1_out4, decoder_1_out5, decoder_1_out6, decoder_1_out7, decoder_2_out1,
       decoder_2_out2, decoder_2_out3, decoder_2_out4, decoder_2_out5, decoder_2_out6, decoder_2_out7,
       nor_1_out, rst;
  wire [2:0] Counter_q;

  Decoder #(.select(3), .enable("false")) decoder_1 (
    .out0(decoder_1_out0), .out1(decoder_1_out1), .out2(decoder_1_out2), .out3(decoder_1_out3),
    .out4(decoder_1_out4), .out5(decoder_1_out5), .out6(decoder_1_out6), .out7(decoder_1_out7),
    .sel(IR_12_15[2:0]));
  nor nor_1 (nor_1_out, AC_Input[0], AC_Input[1], AC_Input[2], AC_Input[3], AC_Input[4], AC_Input[5], AC_Input[6], AC_Input[7], AC_Input[8], AC_Input[9], AC_Input[10], AC_Input[11], AC_Input[12], AC_Input[13], AC_Input[14], AC_Input[15]);
  Decoder #(.select(3), .disabled(0), .enable("false")) decoder_2 (
    .out0(IncPC), .out1(decoder_2_out1), .out2(decoder_2_out2), .out3(decoder_2_out3), .out4(decoder_2_out4),
    .out5(decoder_2_out5), .out6(decoder_2_out6), .out7(decoder_2_out7), .sel(Counter_q));
  Counter #(.width(3), .max('h7)) Counter (.Q(Counter_q), .clk(Clock), .clr(rst));  // open: load, D, count, carry
  and and_1 (StoreM, decoder_1_out1, decoder_2_out4);
  and and_2 (and_2_out, IR_12_15[3], decoder_1_out0, decoder_2_out3);
  and and_3 (and_3_out, decoder_1_out0, decoder_2_out4);
  and and_4 (and_4_out, IR_12_15[3], decoder_1_out1, decoder_2_out3);
  and and_5 (and_5_out, IR_12_15[3], decoder_1_out2, decoder_2_out3);
  and and_6 (and_6_out, decoder_1_out2, decoder_2_out4);
  and and_7 (and_7_out, IR_12_15[3], decoder_1_out3, decoder_2_out3);
  and and_8 (and_8_out, decoder_1_out3, decoder_2_out4);
  and and_9 (and_9_out, IR_12_15[3], decoder_1_out4, decoder_2_out3);
  and and_10 (and_10_out, IR_12_15[3], decoder_1_out5, decoder_2_out3);
  and and_11 (and_11_out, decoder_1_out0, decoder_2_out2);
  and and_12 (and_12_out, IR_12_15[3], decoder_1_out0, decoder_2_out3);
  and and_13 (and_13_out, decoder_1_out1, decoder_2_out2);
  and and_14 (and_14_out, IR_12_15[3], decoder_1_out1, decoder_2_out3);
  and and_15 (and_15_out, decoder_1_out2, decoder_2_out2);
  and and_16 (and_16_out, IR_12_15[3], decoder_1_out2, decoder_2_out3);
  and and_17 (and_17_out, decoder_1_out3, decoder_2_out2);
  and and_18 (and_18_out, IR_12_15[3], decoder_1_out3, decoder_2_out3);
  and and_19 (and_19_out, IR_12_15[3], decoder_1_out4, decoder_2_out2);
  and and_20 (and_20_out, IR_12_15[3], decoder_1_out5, decoder_2_out2);
  and and_21 (and_21_out, decoder_1_out4, decoder_2_out4);
  and and_22 (and_22_out, decoder_1_out5, decoder_2_out4, nor_1_out);
  and and_23 (and_23_out, IR_12_15[3], decoder_1_out4, decoder_2_out3);
  and and_24 (and_24_out, IR_12_15[3], decoder_1_out5, decoder_2_out3);
  and and_25 (and_25_out, decoder_1_out0, decoder_2_out4);
  and and_26 (and_26_out, decoder_1_out2, decoder_2_out4);
  and and_27 (and_27_out, decoder_1_out3, decoder_2_out4);
  and and_28 (and_28_out, decoder_1_out0, decoder_2_out5);
  and and_29 (and_29_out, decoder_1_out2, decoder_2_out5);
  and and_30 (and_30_out, decoder_1_out3, decoder_2_out5);
  and and_31 (and_31_out, decoder_1_out6, decoder_2_out2);
  and and_32 (and_32_out, decoder_1_out7, decoder_2_out2);
  and and_33 (and_33_out, IR_12_15[3], decoder_1_out0, decoder_2_out3);
  and and_34 (and_34_out, decoder_1_out0, decoder_2_out4);
  and and_35 (and_35_out, IR_12_15[3], decoder_1_out1, decoder_2_out3);
  and and_36 (and_36_out, IR_12_15[3], decoder_1_out2, decoder_2_out3);
  and and_37 (and_37_out, decoder_1_out2, decoder_2_out4);
  and and_38 (and_38_out, IR_12_15[3], decoder_1_out3, decoder_2_out3);
  and and_39 (and_39_out, decoder_1_out3, decoder_2_out4);
  and and_40 (and_40_out, IR_12_15[3], decoder_1_out4, decoder_2_out3);
  and and_41 (and_41_out, IR_12_15[3], decoder_1_out5, decoder_2_out3);
  and and_42 (and_42_out, decoder_2_out2, decoder_1_out0);
  and and_43 (and_43_out, decoder_1_out1, decoder_2_out2);
  and and_44 (and_44_out, decoder_1_out2, decoder_2_out2);
  and and_45 (and_45_out, decoder_1_out3, decoder_2_out2);
  and and_46 (and_46_out, IR_12_15[3], decoder_1_out4, decoder_2_out2);
  and and_47 (and_47_out, IR_12_15[3], decoder_1_out5, decoder_2_out2);
  and and_48 (and_48_out, nor_1_out, decoder_1_out5, decoder_2_out4);
  and and_49 (and_49_out, decoder_1_out4, decoder_2_out4);
  and and_50 (SDR, decoder_1_out0, decoder_2_out5);
  and and_51 (SAC, decoder_1_out1, decoder_2_out4);
  and and_52 (and_52_out, decoder_1_out0, decoder_2_out6);
  and and_53 (and_53_out, decoder_1_out1, decoder_2_out5);
  and and_54 (and_54_out, decoder_1_out2, decoder_2_out6);
  and and_55 (and_55_out, decoder_1_out3, decoder_2_out6);
  and and_56 (and_56_out, decoder_1_out4, decoder_2_out5);
  and and_57 (and_57_out, decoder_1_out5, decoder_2_out5);
  and and_58 (and_58_out, decoder_1_out6, decoder_2_out3);
  and and_59 (and_59_out, decoder_1_out7, decoder_2_out3);
  and and_60 (and_60_out, decoder_1_out2, decoder_2_out5);
  and and_61 (and_61_out, decoder_1_out3, decoder_2_out5);
  and and_62 (and_62_out, decoder_1_out6, decoder_2_out2);
  and and_63 (and_63_out, decoder_1_out7, decoder_2_out2);
  and and_64 (and_64_out, decoder_1_out0, decoder_2_out5);
  or or_1 (LoadM, and_2_out, and_3_out, and_4_out, decoder_2_out1, and_5_out, and_6_out, and_7_out, and_8_out, and_9_out, and_10_out);
  or or_2 (EAR, IncPC, and_11_out, and_12_out, and_13_out, and_14_out, and_15_out, and_16_out, and_17_out, and_18_out, and_19_out, and_20_out);
  or or_3 (LoadPC, and_21_out, and_22_out);
  or or_4 (EIR, decoder_2_out1, and_23_out, and_24_out);
  or or_5 (EDR, and_25_out, and_26_out, and_27_out);
  or or_6 (EAC, and_28_out, and_29_out, and_30_out, and_31_out, and_32_out);
  or or_7 (SM, decoder_2_out1, and_33_out, and_34_out, and_35_out, and_36_out, and_37_out, and_38_out, and_39_out, and_40_out, and_41_out);
  or or_8 (SIR, and_42_out, and_43_out, and_44_out, and_45_out, and_46_out, and_47_out, and_48_out, and_49_out);
  or or_9 (rst, and_52_out, and_53_out, and_54_out, and_55_out, and_56_out, and_57_out, and_58_out, and_59_out);
  // Priority_Encoder priority_encoder_1: pin names not known; wires that end beside it: and_60_out, and_61_out, and_62_out, and_63_out, ALU_Control, and_64_out

  assign SPC = IncPC;

  // Notes on the sheet:
  //   Clock: pull=up
  //   this is I
  //   Zac
  //   SroteM
  //   LoadM
  //   EAR
  //   LoadPC
  //   IncPC
  //   EIR
  //   EDR
  //   EAC
  //   SM
  //   SPC
  //   SIR
  //   SDR
  //   SAC
  //   RstSC
  //   ALU add
  //   ALU and
  //   ALU comp
  //   ALU lsl
  //   ALU transmit
endmodule

module test (
  input  in_1,
  input  in_2,
  input  in_3,
  input  in_4
);

  wire clock_1_out, controll_unit_1_eac, controll_unit_1_ear, controll_unit_1_edr, controll_unit_1_eir,
       controll_unit_1_incpc, controll_unit_1_loadm, controll_unit_1_loadpc, controll_unit_1_sac,
       controll_unit_1_sdr, controll_unit_1_sir, controll_unit_1_sm, controll_unit_1_spc,
       controll_unit_1_storem;
  wire [2:0] controll_unit_1_alu_control;

  // Probe on controll_unit_1_loadm
  // Probe on controll_unit_1_ear
  // Probe on controll_unit_1_storem
  // Probe on {in_1, in_2, in_3, in_4}
  // Probe on controll_unit_1_loadpc
  // Probe on controll_unit_1_eir
  // Probe on controll_unit_1_incpc
  // Probe on controll_unit_1_edr
  Controll_Unit controll_unit_1 (
    .IR_12_15({in_1, in_2, in_3, in_4}), .Clock(clock_1_out), .AC_Input(16'h1),
    .ALU_Control(controll_unit_1_alu_control), .StoreM(controll_unit_1_storem),
    .LoadM(controll_unit_1_loadm), .EAR(controll_unit_1_ear), .LoadPC(controll_unit_1_loadpc),
    .IncPC(controll_unit_1_incpc), .EIR(controll_unit_1_eir), .EDR(controll_unit_1_edr),
    .EAC(controll_unit_1_eac), .SM(controll_unit_1_sm), .SPC(controll_unit_1_spc), .SIR(controll_unit_1_sir),
    .SDR(controll_unit_1_sdr), .SAC(controll_unit_1_sac));  // open: EIN, EOUT, SAR, SINR, STMP
  // Probe on controll_unit_1_eac
  // Probe on controll_unit_1_sm
  Clock clock_1 (.out(clock_1_out));
  // Probe on controll_unit_1_sdr
  // Probe on controll_unit_1_spc
  // Probe on controll_unit_1_sac
  // Probe on controll_unit_1_sir
  // Probe on controll_unit_1_alu_control
endmodule
